# Fritzing sketch fake_bomb_schematic (saved by Fritzing 0.9.6b)
stripboards: 1
breadboards: 1

parts:
  Arduino = Arduino Uno (Rev3)
  LCD1 = Adafruit Positive RGB 2x16 LCD
  R1 = Resistor [tolerance=±5% power=0.25 resistance=220 package=THT]
  R2 = Resistor [tolerance=±5% power=0.25 resistance=220 package=THT]
  R3 = Resistor [tolerance=±5% power=0.25 resistance=220 package=THT]
  R4 = Rotary Potentiometer (Small) [maximum_resistance=10kΩ package=THT]

nets:
  N1: Arduino.A0, Arduino.A1, Arduino.A2, Arduino.A3, Arduino.A4/SDA, Arduino.A5/SCL, Arduino.GND, LCD1.no_name_yet#0, LCD1.no_name_yet#4, R4.leg1
  N2: Arduino.D8, R3.Pin_0
  N3: Arduino.D9_PWM, R2.Pin_0
  N4: Arduino.D10_PWM/SS, R1.Pin_0
  N5: Arduino.D11_PWM/MOSI, LCD1.no_name_yet#5
  N6: Arduino.D12/MISO, LCD1.no_name_yet#3
  N7: Arduino.D2, LCD1.no_name_yet#13
  N8: Arduino.D3_PWM, LCD1.no_name_yet#12
  N9: Arduino.D4, LCD1.no_name_yet#11
  N10: Arduino.D5_PWM, LCD1.no_name_yet#10
  N11: Arduino.5V, LCD1.no_name_yet#1, LCD1.no_name_yet#14, R4.leg2
  N12: LCD1.no_name_yet#2, R4.wiper
  N13: LCD1.no_name_yet#15, R3.Pin_1
  N14: LCD1.no_name_yet#16, R2.Pin_1
  N15: LCD1.no_name_yet#17, R1.Pin_1

notes:
  wires to cut

custom parts:
  Adafruit Positive RGB 2x16 LCD: Adafruit Positive 2x16 LCD Display with RGB Backlight
